# Fritzing sketch ModuloPrincipal (saved by Fritzing 0.8.7b)
breadboards: 1

parts:
  P9 = 46 Pins Beagle [form="♂ (male)" package=THT]
  U1 = Voltage Regulator - 5V [package="TO220 [THT]"]
  C1 = Electrolytic Capacitor [capacitance=220µF voltage=16V package="100 mil [THT, electrolytic]"]
  C2 = Electrolytic Capacitor [capacitance=33µF package="100 mil [THT, electrolytic]"]
  C3 = Ceramic Capacitor [capacitance=0.1µF package="100 mil [THT, multilayer]"]
  C4 = Ceramic Capacitor [capacitance=0.1µF package="100 mil [THT, multilayer]"]
  Vin = female pin header, 2 pins [form="♀ (female)"]
  D1 = Diode [package=diode-1n4001]
  CD4051B = IC, DIP package, 16 pins [chip_label=CD4051B]
  R5 = Resistor [tolerance=±5% resistance=470 package=THT]
  Analog_Inputs = double row female pin header, 16 pins [form="♀ (female)"]
  LED_Outputs = double row female pin header, 8 pins [form="♀ (female)"]
  R6 = Resistor [tolerance=±5% resistance=470 package=THT]
  R7 = Resistor [tolerance=±5% resistance=470 package=THT]
  R8 = Resistor [tolerance=±5% resistance=470 package=THT]
  Digital_Inputs = double row female pin header, 12 pins [form="♀ (female)"]
  P8 = 46 Pins Beagle [form="♂ (male)" package=THT]

nets:
  3.3V: P9.pin3, P9.pin4, CD4051B.pin16, LED_Outputs.pin1, LED_Outputs.pin2, LED_Outputs.pin3, LED_Outputs.pin4, Digital_Inputs.pin7, Digital_Inputs.pin8, Digital_Inputs.pin9, Digital_Inputs.pin10, Digital_Inputs.pin11, Digital_Inputs.pin12
  5V: P9.pin5, P9.pin6
  p9-11: P9.pin11, Digital_Inputs.pin6
  p9-12: P9.pin12, R5.Pin_1
  p9-13: P9.pin13, Digital_Inputs.pin5
  p9-14: P9.pin14, R6.Pin_1
  p9-15: P9.pin15, Digital_Inputs.pin4
  p9-16: P9.pin16, R7.Pin_1
  p9-21: P9.pin21, Digital_Inputs.pin3
  p9-22: P9.pin22
  p9-23: P9.pin23, Digital_Inputs.pin2
  N1: P9.pin27, CD4051B.pin11
  N2: P9.pin30, CD4051B.pin10
  N3: P9.pin32, Analog_Inputs.pin1
  N4: P9.pin33, Analog_Inputs.pin7
  N5: P9.pin34, Analog_Inputs.pin2
  N6: P9.pin35, CD4051B.pin3
  N7: P9.pin36, Analog_Inputs.pin8
  N8: P9.pin37, Analog_Inputs.pin5
  N9: P9.pin38, Analog_Inputs.pin6
  N10: P9.pin39, Analog_Inputs.pin3
  N11: P9.pin40, Analog_Inputs.pin4
  p9-41: P9.pin41, Digital_Inputs.pin1
  N12: P9.pin42, CD4051B.pin9
  GND: P9.pin43, P9.pin44, P9.pin45, P9.pin46
  N13: U1.input_voltage, C1.+, C3.1, D1.C
  N14: U1.GND, C1.-, C2.-, C3.0, C4.0, Vin.pin2
  N15: U1.output_voltage, C2.+, C4.1
  N16: Vin.pin1, D1.A
  N17: CD4051B.pin1, Analog_Inputs.pin13
  N18: CD4051B.pin2, Analog_Inputs.pin15
  N19: CD4051B.pin4, Analog_Inputs.pin16
  N20: CD4051B.pin5, Analog_Inputs.pin14
  GND2: CD4051B.pin6, CD4051B.pin7, CD4051B.pin8, P8.pin45, P8.pin46
  N21: CD4051B.pin12, Analog_Inputs.pin12
  N22: CD4051B.pin13, Analog_Inputs.pin9
  N23: CD4051B.pin14, Analog_Inputs.pin10
  N24: CD4051B.pin15, Analog_Inputs.pin11
  N25: R5.Pin_0, LED_Outputs.pin5
  N26: LED_Outputs.pin6, R6.Pin_0
  N27: LED_Outputs.pin7, R7.Pin_0
  N28: LED_Outputs.pin8, R8.Pin_0

custom parts:
  46 Pins Beagle: 46 pins beagle
