# Fritzing sketch ModuloPrincipalMinimo (saved by Fritzing 0.8.7b)
circuit board: 3.28233cm x 6.01765cm
breadboards: 1

parts:
  U1 = Voltage Regulator - 5V [package="TO220 [THT]"]
  C1 = Electrolytic Capacitor [capacitance=220µF voltage=16V package="100 mil [THT, electrolytic]"]
  C2 = Electrolytic Capacitor [capacitance=33µF package="100 mil [THT, electrolytic]"]
  C3 = Ceramic Capacitor [capacitance=0.1µF package="100 mil [THT, multilayer]"]
  C4 = Ceramic Capacitor [capacitance=0.1µF package="100 mil [THT, multilayer]"]
  Vin = female pin header, 2 pins [form="♀ (female)"]
  CD4051B = IC, DIP package, 16 pins [chip_label=CD4051B]
  R5 = Resistor [tolerance=±5% resistance=470 package=THT]
  R6 = Resistor [tolerance=±5% resistance=470 package=THT]
  R7 = Resistor [tolerance=±5% resistance=470 package=THT]
  R8 = Resistor [tolerance=±5% resistance=470 package=THT]
  P8 = 46 Pins Beagle [form="♂ (male)" package=THT]  # not connected
  Analog_Inputs = female pin header, 8 pins [form="♀ (female)"]
  LED_Outputs = female pin header, 4 pins [form="♀ (female)"]
  P9 = double row male pin header, 44 pins [form="♂ (male)"]

nets:
  N1: U1.input_voltage, C1.+, C3.1, Vin.pin1
  GND: U1.GND, C1.-, C2.-, C3.0, C4.0, Vin.pin2, CD4051B.pin6, CD4051B.pin7, CD4051B.pin8, P9.pin41, P9.pin42, P9.pin43, P9.pin44
  5V: U1.output_voltage, C2.+, C4.1, P9.pin3, P9.pin4
  N2: CD4051B.pin1, Analog_Inputs.pin5
  N3: CD4051B.pin2, Analog_Inputs.pin7
  N4: CD4051B.pin3, P9.pin33
  N5: CD4051B.pin4, Analog_Inputs.pin8
  N6: CD4051B.pin5, Analog_Inputs.pin6
  N7: CD4051B.pin9, P9.pin40
  N8: CD4051B.pin10, P9.pin28
  N9: CD4051B.pin11, P9.pin25
  N10: CD4051B.pin12, Analog_Inputs.pin4
  N11: CD4051B.pin13, Analog_Inputs.pin1
  N12: CD4051B.pin14, Analog_Inputs.pin2
  N13: CD4051B.pin15, Analog_Inputs.pin3
  3.3V: CD4051B.pin16, P9.pin1, P9.pin2
  N14: R5.Pin_0, LED_Outputs.pin1
  p9-12: R5.Pin_1, P9.pin10
  N15: R6.Pin_0, LED_Outputs.pin2
  p9-14: R6.Pin_1, P9.pin12
  N16: R7.Pin_0, LED_Outputs.pin3
  p9-16: R7.Pin_1, P9.pin14
  N17: R8.Pin_0, LED_Outputs.pin4
  p9-18: R8.Pin_1

notes:
  Ojo, P8 Aqui es de 44 pines, no 46. Los 2 primeros en la Beagle quedan desconectados. Los pines marcados aqui no corresponden al numero de la Beagle.

custom parts:
  46 Pins Beagle: 46 pins beagle
